# Fritzing sketch senior (saved by Fritzing 0.9.3b)
breadboards: 2

parts:
  Part1 = Arduino Due (Rev2b)
  Part2 = Arduino Due (Rev2b)
  Part3 = HX711 Weighing Sensor Module
  R1 = Resistor [tolerance=±5% resistance=220 package="0805 [SMD]"]
  R2 = Resistor [tolerance=±5% resistance=220 package="0805 [SMD]"]
  R3 = Resistor [tolerance=±5% resistance=220 package="0805 [SMD]"]
  R4 = Resistor [tolerance=±5% resistance=220 package="0805 [SMD]"]
  Part5 = HX711 Weighing Sensor Module
  R17 = Resistor [tolerance=±5% resistance=220 package="0805 [SMD]"]
  R18 = Resistor [tolerance=±5% resistance=220 package="0805 [SMD]"]
  R19 = Resistor [tolerance=±5% resistance=220 package="0805 [SMD]"]
  R20 = Resistor [tolerance=±5% resistance=220 package="0805 [SMD]"]
  Part8 = Adafruit Datalogger Shield v1 [part_number="Adafruit #1141"]
  GY1 = MPU-6050 Board GY-521 [form="♀ (female)" package=THT]

nets:
  N1: Part1.A0, Part3.CK/TX
  N2: Part1.A1, Part3.DO/RX
  N3: Part1.A2, Part5.CK/TX
  N4: Part1.A3, Part5.DO/RX
  N5: Part1.D20/SDA3, Part2.D20/SDA3, GY1.pin4
  N6: Part1.D21/SCL3, Part2.D21/SCL3, GY1.pin3
  VCC: Part1.5V, Part3.VCC, Part5.VCC, GY1.pin1
  GND: Part1.GND, Part3.GND, Part5.GND, GY1.pin2
  N7: Part1.D2_PWM, GY1.pin8
  N8: Part3.E+, R3.Pin_0, R4.Pin_1
  N9: Part3.E-, R1.Pin_1, R2.Pin_0
  N10: Part3.A+, R2.Pin_1, R3.Pin_1
  N11: Part3.A-, R1.Pin_0, R4.Pin_0
  N12: Part5.E+, R17.Pin_0, R20.Pin_1
  N13: Part5.E-, R18.Pin_1, R19.Pin_0
  N14: Part5.A+, R17.Pin_1, R19.Pin_1
  N15: Part5.A-, R18.Pin_0, R20.Pin_0
  N16: Part8.SCK, Part8.N$55
  N17: Part8.MISO, Part8.N$48
  N18: Part8.MOSI, Part8.N$40

notes:
  Resistors are in place of Strain gauges in a Wheatstone Bridge configuration.
  Master I2C device with data logger shield
  Slave I2C device with sensors attached

custom parts:
  Adafruit Datalogger Shield v1: Here's a handy Arduino shield: we've had a lot of people looking for a dedicated and well-designed data logging shield. We worked hard to engineer an inexpensive but well-rounded design. Not only is it easy to assemble and customize, it also comes with great documentation and libraries. New! we now are carrying an 'assembled' version of this shield, with all the components pre-soldered. NOTE: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
  MPU-6050 Board GY-521: Acelerometro y Giroscopio MPU-6050 Board GY-521
